// Logisim project access_control_lock.circ as structural Verilog: 1 circuit, main circuit main
module main (
  input  D0,
  input  D1,
  input  D2,
  input  M
);

  wire and_1_out, and_2_out, not_1_out, not_2_out, not_3_out, not_4_out, or_1_out;

  not not_1 (not_1_out, D1);
  not not_2 (not_2_out, M);
  not not_3 (not_3_out, D2);
  and and_1 (and_1_out, D0, not_1_out, D2, not_2_out);
  and and_2 (and_2_out, D0, D1, not_3_out, M);
  LED led_1 (.in(or_1_out));
  or or_1 (or_1_out, and_1_out, and_2_out);
  not not_4 (not_4_out, or_1_out);
  LED led_2 (.in(not_4_out));

  // Notes on the sheet:
  //   Unlock
  //   Warning
endmodule
